// Logisim project alu.circ as structural Verilog: 5 circuits, main circuit main
module main (
  input  [31:0] X,
  input  [31:0] Y,
  input  [5:0] Switch__S,
  output Signed_Overflow,
  output [31:0] RESULT,
  output Equal
);

  wire add_overflow_1_overflow, and_2_out, and_4_out, and_5_out, bitpal_1_out_2, comparator_1_lt,
       comparator_2_lt, comparator_3_eq, comparator_4_eq, not_1_out, or_1_out, or_4_out, or_5_out,
       overflow___add, overflow___sub, subtract_overflow_1_overflow;
  wire [3:2] or_2_out;
  wire [4:0] bit_extender_1_out, bit_extender_2_out, bit_extender_3_out;
  wire [31:0] add, addu, \and , bitpal, lfsr, \or , sll, slt, sltu, sra, srl, sub, subu;

  Bit_Extender #(.in_width(32), .out_width(5)) bit_extender_1 (.in(Y), .out(bit_extender_1_out));
  Bit_Extender #(.in_width(32), .out_width(5)) bit_extender_2 (.in(Y), .out(bit_extender_2_out));
  Bit_Extender #(.in_width(32), .out_width(5)) bit_extender_3 (.in(Y), .out(bit_extender_3_out));
  Adder #(.width(32)) adder_1 (.a(X), .b(Y), .out(add), .cout(overflow___add));  // open: cin
  Adder #(.width(32)) adder_2 (.a(X), .b(Y), .out(addu));  // open: cin, cout
  Subtractor #(.width(32)) subtractor_1 (.a(X), .b(Y), .out(sub), .bout(overflow___sub));  // open: bin
  Subtractor #(.width(32)) subtractor_2 (.a(X), .b(Y), .out(subu));  // open: bin, bout
  Shifter #(.width(32)) shifter_1 (.in(X), .\dist (bit_extender_1_out), .out(sll));
  Shifter #(.width(32), .shift("lr")) shifter_2 (.in(X), .\dist (bit_extender_2_out), .out(srl));
  Shifter #(.width(32), .shift("ar")) shifter_3 (.in(X), .\dist (bit_extender_3_out), .out(sra));
  or or_1 (or_1_out, Switch__S[2], Switch__S[3]);
  and and_1 (or_2_out[3], or_1_out, Switch__S[5]);
  not not_1 (not_1_out, Switch__S[3]);
  and and_2 (and_2_out, not_1_out, Switch__S[5]);
  or or_2 (or_2_out[2], and_2_out, Switch__S[4]);
  assign \and  = X & Y;  // AND_Gate and_3, 32 bits wide
  assign \or  = X | Y;  // OR_Gate or_3, 32 bits wide
  Comparator #(.width(32)) comparator_1 (.a(X), .b(Y), .eq(Equal), .lt(comparator_1_lt));  // open: gt
  Comparator #(.width(32), .mode("unsigned")) comparator_2 (.a(X), .b(Y), .lt(comparator_2_lt));  // open: gt, eq
  bitpal bitpal_1 (.in_1(X), .out_2(bitpal_1_out_2));
  lfsr lfsr_1 (.in_1(X), .out(lfsr));
  assign slt = {{31{1'b0}}, comparator_1_lt};  // Bit_Extender bit_extender_4
  assign sltu = {{31{1'b0}}, comparator_2_lt};  // Bit_Extender bit_extender_5
  assign bitpal = {{31{1'b0}}, bitpal_1_out_2};  // Bit_Extender bit_extender_6
  Comparator #(.width(6)) comparator_3 (.a(6'b100010), .b(Switch__S), .eq(comparator_3_eq));  // open: gt, lt
  subtract_overflow subtract_overflow_1 (.X_IN(X), .Y_IN(Y), .RESULT_IN(sub), .overflow(subtract_overflow_1_overflow));
  add_overflow add_overflow_1 (.X_IN(X), .Y_IN(Y), .RESULT_IN(add), .overflow(add_overflow_1_overflow));
  Comparator #(.width(6)) comparator_4 (.a(6'b100000), .b(Switch__S), .eq(comparator_4_eq));  // open: gt, lt
  or or_4 (or_4_out, overflow___sub, subtract_overflow_1_overflow);
  or or_5 (or_5_out, add_overflow_1_overflow, overflow___add);
  and and_4 (and_4_out, comparator_3_eq, or_4_out);
  and and_5 (and_5_out, or_5_out, comparator_4_eq);
  Multiplexer #(.select(4), .width(32), .enable("false")) multiplexer_1 (
    .in0(sll), .in2(srl), .in3(sra), .in4(add), .in5(addu), .in6(sub), .in7(subu), .in10(slt), .in11(sltu),
    .in12(\and ), .in13(\or ), .in14(bitpal), .in15(lfsr), .out(RESULT), .sel({or_2_out, Switch__S[1:0]}));  // open: in1, in8, in9
  or or_6 (Signed_Overflow, and_4_out, and_5_out);

  // Other names for the same wires on the sheet: eq = Equal; overflow_Y = Signed_Overflow

  // Notes on the sheet:
  //   INPUTS to your circuit
  //   INPUT to your circuit
  //   DON'T CHANGE THE INPUTS AND OUTPUTS! IF YOU DO SO, YOU NEED TO MAKE SURE THE PINS ARE IN THE RIGHT PLACES!
  //   OUTPUTS of your circuit
endmodule

module bitpal (
  input  [31:0] in_1,
  output out_2
);

  Comparator #(.width(16)) comparator_1 (
    .a({in_1[0], in_1[1], in_1[2], in_1[3], in_1[4], in_1[5], in_1[6], in_1[7], in_1[8], in_1[9], in_1[10], in_1[11], in_1[12], in_1[13], in_1[14], in_1[15]}),
    .b(in_1[31:16]), .eq(out_2));  // open: gt, lt
endmodule

module lfsr (
  input  [31:0] in_1,
  output [31:0] out
);

  wire xor_1_out, xor_2_out, xor_3_out;
  wire [31:0] bit_extender_1_out, shifter_1_out, shifter_2_out;

  xor xor_1 (xor_1_out, in_1[0], in_1[2]);
  xor xor_2 (xor_2_out, xor_1_out, in_1[3]);
  xor xor_3 (xor_3_out, xor_2_out, in_1[5]);
  assign bit_extender_1_out = {{31{1'b0}}, xor_3_out};  // Bit_Extender bit_extender_1
  Shifter #(.width(32)) shifter_1 (.in(bit_extender_1_out), .\dist ({5{1'b1}}), .out(shifter_1_out));
  Shifter #(.width(32), .shift("lr")) shifter_2 (.in(in_1), .\dist (5'b00001), .out(shifter_2_out));
  assign out = shifter_1_out | shifter_2_out;  // OR_Gate or_1, 32 bits wide
endmodule

module add_overflow (
  input  [31:0] X_IN,
  input  [31:0] Y_IN,
  input  [31:0] RESULT_IN,
  output overflow
);

  wire xnor_1_out, xor_1_out;

  xor xor_1 (xor_1_out, Y_IN[31], RESULT_IN[31]);
  xnor xnor_1 (xnor_1_out, X_IN[31], Y_IN[31]);
  and and_1 (overflow, xnor_1_out, xor_1_out);
endmodule

module subtract_overflow (
  input  [31:0] X_IN,
  input  [31:0] Y_IN,
  input  [31:0] RESULT_IN,
  output overflow
);

  wire xnor_1_out, xor_1_out;

  xor xor_1 (xor_1_out, X_IN[31], Y_IN[31]);
  xnor xnor_1 (xnor_1_out, Y_IN[31], RESULT_IN[31]);
  and and_1 (overflow, xor_1_out, xnor_1_out);
endmodule
