// Logisim project mem.circ as structural Verilog: 2 circuits, main circuit main
module main (
  input  [31:0] Data_Mem_Addr,
  input  [31:0] Data_Mem_In,
  input  ACCESS_BYTE,
  input  MEM_WRITE,
  input  CLOCK,
  output [31:0] Data_Mem_Out
);

  wire not_1_out;
  wire [23:0] Address, bit_extender_1_out;
  wire [31:0] controlled_buffer_1_out, shifter_1_out;

  Shifter #(.width(32), .shift("lr")) shifter_1 (.in(Data_Mem_Addr), .\dist (5'b00010), .out(shifter_1_out));
  Bit_Extender #(.in_width(32), .out_width(24)) bit_extender_1 (.in(shifter_1_out), .out(bit_extender_1_out));
  Subtractor #(.width(24)) subtractor_1 (.a(bit_extender_1_out), .b(24'h4000), .out(Address));  // open: bin, bout
  assign controlled_buffer_1_out = MEM_WRITE ? Data_Mem_In : 32'bz;  // Controlled_Buffer controlled_buffer_1
  RAM #(.addrWidth(24), .dataWidth(32)) ram_1 (
    .addr(Address), .data(controlled_buffer_1_out), .sel(1'b1), .clk(CLOCK), .ld(not_1_out), .clr(1'b0));
  not not_1 (not_1_out, MEM_WRITE);
  word_byte word_byte_1 (
    .Data_In(controlled_buffer_1_out), .Byte_Num(Data_Mem_Addr[1:0]), .Use_Byte(ACCESS_BYTE),
    .Write(MEM_WRITE), .Data_Out(Data_Mem_Out));

  // Other names for the same wires on the sheet: Byte = ACCESS_BYTE; Clk = CLOCK; Data_In[31:0] = Data_Mem_In;
  //   Byte_Num[1:0] = Data_Mem_Addr[1:0]; Data_Out[31:0] = Data_Mem_Out; Wr = MEM_WRITE

  // Notes on the sheet:
  //   These are INPUTS to the circuit
  //   These are INPUTS to the circuit
  //   DO NOT CHANGE THE LOCATIONS OF THE INPUTS/OUTPUTS! IF YOU DO SO, YOU NEED TO MAKE SURE THE PINS ARE AT THE RIGHT PLACE!
  //   Yet again, the clock is not an actual clock, but an input, one that will be driven from a higher circuit
  //   This is an OUTPUT to the circuit
endmodule

module word_byte (
  input  [31:0] Data_In,
  input  [1:0] Byte_Num,
  input  Use_Byte,
  input  Write,
  output [31:0] Data_Out
);

  wire and_2_out, not_1_out;
  wire [4:0] bit_extender_1_out, shifter_1_out;
  wire [31:0] and_1_out, multiplexer_1_out, multiplexer_2_out, shifter_2_out;

  Multiplexer #(.select(2), .width(32), .enable("false")) multiplexer_1 (
    .in0(32'hff), .in1(32'hff00), .in2(32'hff0000), .in3(32'hff000000), .out(multiplexer_1_out),
    .sel(Byte_Num));
  assign and_1_out = Data_In & multiplexer_1_out;  // AND_Gate and_1, 32 bits wide
  Multiplexer #(.width(32), .enable("false")) multiplexer_2 (
    .in0(Data_In), .in1(and_1_out), .out(multiplexer_2_out), .sel(Use_Byte));
  assign bit_extender_1_out = {{3{1'b0}}, Byte_Num};  // Bit_Extender bit_extender_1
  Shifter #(.width(5)) shifter_1 (.in(bit_extender_1_out), .\dist (3'b011), .out(shifter_1_out));
  Shifter #(.width(32), .shift("lr")) shifter_2 (.in(multiplexer_2_out), .\dist (shifter_1_out), .out(shifter_2_out));
  not not_1 (not_1_out, Write);
  Multiplexer #(.width(32), .enable("false")) multiplexer_3 (
    .in0(multiplexer_2_out), .in1(shifter_2_out), .out(Data_Out), .sel(and_2_out));
  and and_2 (and_2_out, not_1_out, Use_Byte);

  // Other names for the same wires on the sheet: UseByte = Use_Byte
endmodule
