// Logisim project cpu.circ as structural Verilog: 8 circuits, main circuit main
module main (
  input  [31:0] RS_READ_VALUE,
  input  [31:0] RT_READ_VALUE,
  input  [31:0] INSTRUCTION,
  input  CLOCK,
  input  RESET,
  output [31:0] t0,
  output [31:0] t1,
  output [31:0] t2,
  output [31:0] t3,
  output [4:0] RS,
  output [4:0] RT,
  output [4:0] Write_Register,
  output [31:0] RD_WRITE_VALUE,
  output RD_WRITE_ENABLE,
  output [23:0] FETCH_ADDRESS
);

  wire ALU_signed_overflow, ALUSrc, and_3_out, and_5_out, and_7_out, beq, Branch, Branch_Taken,
       comparator_1_eq, comparator_4_eq, comparator_5_eq, control_1_jump, control_1_regwr, enable_run, Equal,
       ExtOp, Jal, Jr, Jump, MemToReg, MemWr, not_1_out, not_2_out, not_3_out, or_1_out, or_3_out, or_4_out,
       RegDest, RegWr, Rtype, writetocorrectreg_3_wenable_rf;
  wire [1:0] bit_extender_4_out, bit_extender_5_out, bit_extender_6_out;
  wire [4:0] multiplexer_5_out, rdWrite, writetocorrectreg_1_formatregnum, writetocorrectreg_2_formatregnum;
  wire [5:0] ALUctl, Funct, Opcode;
  wire [15:0] imm;
  wire [23:0] adder_2_out, bit_extender_1_out, bit_extender_7_out, BranchAddr, JumpAddr, JumpInst,
       multiplexer_3_out, multiplexer_4_out, PC___1, subtractor_1_out;
  wire [31:0] ALU_Result, bit_extender_8_out, correctregchoice_1_correct_read_reg,
       correctregchoice_2_correct_read_reg, correctregchoice_3_correct_read_reg, ExtendedImm,
       MEM_data_mem_out, MemWrData, multiplexer_2_out, multiplexer_7_out, multiplexer_8_out, rs_rf, rt_rf,
       shamtuser_1_x__rs_rt;

  Multiplexer #(.width(5), .enable("false")) multiplexer_1 (
    .in0(rdWrite), .in1({5{1'b1}}), .out(Write_Register), .sel(Jal));
  and and_1 (RD_WRITE_ENABLE, enable_run, RegWr);
  or or_1 (or_1_out, Jump, Branch_Taken);
  Multiplexer #(.width(32), .enable("false")) multiplexer_2 (
    .in0(INSTRUCTION), .in1({32{1'b0}}), .out(multiplexer_2_out), .sel(or_1_out));
  Comparator #(.width(6), .mode("unsigned")) comparator_1 (
    .a(6'b001000), .b(Funct), .eq(comparator_1_eq));  // open: gt, lt
  Register #(.width(32)) register_1 (.D(multiplexer_2_out), .Q({Opcode, RS, RT, imm}), .clk(CLOCK));  // open: en, clr
  and and_2 (Jr, comparator_1_eq, Rtype);
  CorrectRegChoice correctregchoice_1 (
    .from_run_circ(RS_READ_VALUE), .from_regfile(rs_rf), .reg_num(RS),
    .correct_read_reg(correctregchoice_1_correct_read_reg));
  Bit_Extender #(.in_width(32), .out_width(24)) bit_extender_1 (
    .in(correctregchoice_1_correct_read_reg), .out(bit_extender_1_out));
  Multiplexer #(.width(24), .enable("false")) multiplexer_3 (
    .in0(BranchAddr), .in1(JumpAddr), .out(multiplexer_3_out), .sel(Jump));
  Register #(.width(24)) register_2 (.D(multiplexer_3_out), .Q(FETCH_ADDRESS), .clk(CLOCK));  // open: en, clr
  Bit_Extender #(.in_width(32), .out_width(24)) bit_extender_2 (.in({Opcode, RS, RT, imm}), .out(JumpInst));
  Multiplexer #(.width(24), .enable("false")) multiplexer_4 (
    .in0(JumpInst), .in1(bit_extender_1_out), .out(multiplexer_4_out), .sel(Jr));
  Bit_Extender #(.in_width(16), .out_width(6)) bit_extender_3 (.in(imm), .out(Funct));
  Comparator #(.width(6), .mode("unsigned")) comparator_2 (.a(Opcode), .b(6'b000011), .eq(Jal));  // open: gt, lt
  Comparator #(.width(6), .mode("unsigned")) comparator_3 (.a(Opcode), .b(6'b000100), .eq(beq));  // open: gt, lt
  Subtractor #(.width(24)) subtractor_1 (
    .a(multiplexer_4_out), .b(24'h100000), .out(subtractor_1_out));  // open: bin, bout
  Adder #(.width(24)) adder_1 (.a(FETCH_ADDRESS), .b(24'h1), .out(PC___1));  // open: cin, cout
  WriteToCorrectReg writetocorrectreg_1 (
    .RegNum(RS), .FormatRegNum(writetocorrectreg_1_formatregnum));  // open: wEnable_rf, wEnable_run
  WriteToCorrectReg writetocorrectreg_2 (
    .RegNum(RT), .FormatRegNum(writetocorrectreg_2_formatregnum));  // open: wEnable_rf, wEnable_run
  WriteToCorrectReg writetocorrectreg_3 (
    .RegNum(multiplexer_5_out), .FormatRegNum(rdWrite), .wEnable_rf(writetocorrectreg_3_wenable_rf),
    .wEnable_run(enable_run));
  Multiplexer #(.width(5), .enable("false")) multiplexer_5 (
    .in0(RT), .in1(imm[15:11]), .out(multiplexer_5_out), .sel(RegDest));
  control control_1 (
    .opcode(Opcode), .RegDest(RegDest), .ExtOp(ExtOp), .RegWr(control_1_regwr), .ALUSrc(ALUSrc),
    .MemWr(MemWr), .MemToReg(MemToReg), .Branch(Branch), .Jump(control_1_jump), .opALU1(Rtype));
  // Probe on subtractor_1_out
  Shifter #(.width(24), .shift("lr")) shifter_1 (.in(subtractor_1_out), .\dist (5'b00010), .out(JumpAddr));
  Bit_Extender #(.in_width(5), .out_width(2)) bit_extender_4 (
    .in(writetocorrectreg_1_formatregnum), .out(bit_extender_4_out));
  Bit_Extender #(.in_width(5), .out_width(2)) bit_extender_5 (
    .in(writetocorrectreg_2_formatregnum), .out(bit_extender_5_out));
  Bit_Extender #(.in_width(5), .out_width(2)) bit_extender_6 (.in(rdWrite), .out(bit_extender_6_out));
  // Probe on JumpAddr
  not not_1 (not_1_out, Jr);
  or or_2 (Jump, Jr, control_1_jump);
  ALUCtr aluctr_1 (.opcode(Opcode), .funct(Funct), .R_type(Rtype), .ALUctl(ALUctl));
  regfile_main RegFile (
    .Read_register_1(bit_extender_4_out), .Read_register_2(bit_extender_5_out),
    .write_register(bit_extender_6_out), .write_data(RD_WRITE_VALUE), .t0_Value(t0), .t1_Value(t1),
    .t2_Value(t2), .t3_Value(t3), .RegWrite(and_3_out), .clock(CLOCK), .Read_Data_1(rs_rf),
    .Read_Data_2(rt_rf));
  and and_3 (and_3_out, writetocorrectreg_3_wenable_rf, RegWr);
  and and_4 (RegWr, not_1_out, control_1_regwr);
  Comparator #(.width(6), .mode("unsigned")) comparator_4 (
    .a(6'b100000), .b(Opcode), .eq(comparator_4_eq));  // open: gt, lt
  Comparator #(.width(6), .mode("unsigned")) comparator_5 (
    .a(Opcode), .b(6'b100100), .eq(comparator_5_eq));  // open: gt, lt
  Bit_Extender #(.in_width(32), .out_width(24)) bit_extender_7 (.in(ExtendedImm), .out(bit_extender_7_out));
  CorrectRegChoice correctregchoice_2 (
    .from_run_circ(RT_READ_VALUE), .from_regfile(rt_rf), .reg_num(RT),
    .correct_read_reg(correctregchoice_2_correct_read_reg));
  or or_3 (or_3_out, comparator_4_eq, comparator_5_eq);
  Adder #(.width(24)) adder_2 (.a(FETCH_ADDRESS), .b(bit_extender_7_out), .out(adder_2_out));  // open: cin, cout
  and and_5 (and_5_out, Equal, beq);
  CorrectRegChoice correctregchoice_3 (
    .from_run_circ(RS_READ_VALUE), .from_regfile(rs_rf), .reg_num(RS),
    .correct_read_reg(correctregchoice_3_correct_read_reg));
  sign_zero_extended sign_zero_extended_1 (.Immediate(imm), .ExtOp(ExtOp), .opcode(Opcode), .ExtImm(ExtendedImm));
  mem_main MEM (
    .Data_Mem_Addr(ALU_Result), .Data_Mem_In(MemWrData), .ACCESS_BYTE(or_3_out), .MEM_WRITE(MemWr),
    .CLOCK(CLOCK), .Data_Mem_Out(MEM_data_mem_out));
  Multiplexer #(.width(24), .enable("false")) multiplexer_6 (
    .in0(PC___1), .in1(adder_2_out), .out(BranchAddr), .sel(Branch_Taken));
  and and_6 (Branch_Taken, or_4_out, Branch);
  or or_4 (or_4_out, and_5_out, and_7_out);
  shamtUser shamtuser_1 (
    .Rtype(Rtype), .funct(Funct), .RT(correctregchoice_2_correct_read_reg), .shamt(imm[10:6]),
    .RS(correctregchoice_3_correct_read_reg), .Y__RT_Shamt(MemWrData), .X__RS_RT(shamtuser_1_x__rs_rt));
  Multiplexer #(.width(32), .enable("false")) multiplexer_7 (
    .in0(MemWrData), .in1(ExtendedImm), .out(multiplexer_7_out), .sel(ALUSrc));
  Multiplexer #(.width(32), .enable("false")) multiplexer_8 (
    .in0(ALU_Result), .in1(MEM_data_mem_out), .out(multiplexer_8_out), .sel(MemToReg));
  and and_7 (and_7_out, not_2_out, not_3_out);
  not not_2 (not_2_out, Equal);
  not not_3 (not_3_out, beq);
  assign bit_extender_8_out = {{8{1'b0}}, PC___1};  // Bit_Extender bit_extender_8
  LED led_1 (.in(ALU_signed_overflow));
  alu_main ALU (
    .Switch__S(ALUctl), .X(shamtuser_1_x__rs_rt), .Equal(Equal), .RESULT(ALU_Result),
    .Signed_Overflow(ALU_signed_overflow), .Y(multiplexer_7_out));
  Multiplexer #(.width(32), .enable("false")) multiplexer_9 (
    .in0(multiplexer_8_out), .in1(bit_extender_8_out), .out(RD_WRITE_VALUE), .sel(Jal));

  // Other names for the same wires on the sheet: Shamt[4:0] = imm[10:6]; rd[4:0] = imm[15:11]; Clk = CLOCK;
  //   PC[23:0] = FETCH_ADDRESS; RegWrData[31:0] = RD_WRITE_VALUE; rs_run[31:0] = RS_READ_VALUE;
  //   rt_run[31:0] = RT_READ_VALUE

  // Notes on the sheet:
  //   These are outputs/inputs from run.circ
  //   JR
  //   Instruction Fetch
  //   These are outputs to run.circ
  //   Decode / Register Read
  //   Next PC Logic
  //   Load Byte?
  //   Memory
  //   Deals with Shifts
  //   Execute
  //   Register Wrtie
endmodule

module control (
  input  [5:0] opcode,
  output RegDest,
  output ExtOp,
  output RegWr,
  output ALUSrc,
  output MemWr,
  output MemToReg,
  output Branch,
  output Jump,
  output opALU1
);

  wire and_1_out, and_3_out, comparator_2_eq, nor_1_out, not_1_out, not_2_out, not_3_out, not_4_out,
       not_5_out, not_6_out, not_7_out, not_8_out, not_9_out, not_10_out, not_11_out, not_12_out, not_13_out,
       not_14_out, not_15_out, not_16_out, not_17_out, not_18_out, not_19_out, not_20_out, not_21_out,
       Or_Jal_out, Ori, xor_1_out;

  Comparator #(.width(6), .mode("unsigned")) comparator_1 (.a(opcode), .b(6'b001101), .eq(Ori));  // open: gt, lt
  Comparator #(.width(6), .mode("unsigned")) comparator_2 (
    .a(opcode), .b(6'b000011), .eq(comparator_2_eq));  // open: gt, lt
  xor xor_1 (xor_1_out, opcode[3], opcode[5]);
  not not_1 (not_1_out, opcode[2]);
  not not_2 (not_2_out, opcode[3]);
  not not_3 (not_3_out, opcode[4]);
  not not_4 (not_4_out, opcode[5]);
  not not_5 (not_5_out, opcode[5]);
  not not_6 (not_6_out, opcode[4]);
  not not_7 (not_7_out, opcode[2]);
  and and_1 (and_1_out, not_5_out, not_6_out, opcode[3], not_7_out, opcode[1], opcode[0]);
  or Or_Jal (Or_Jal_out, comparator_2_eq, xor_1_out);
  and and_2 (Jump, opcode[1], not_1_out, not_2_out, not_3_out, not_4_out);
  not not_8 (not_8_out, opcode[5]);
  not not_9 (not_9_out, opcode[4]);
  and and_3 (and_3_out, not_8_out, not_9_out, opcode[3], opcode[2], not_13_out, not_12_out);
  or or_1 (ALUSrc, opcode[3], opcode[5]);
  and and_4 (MemWr, opcode[3], opcode[5]);
  not not_10 (not_10_out, opcode[3]);
  and and_5 (Branch, opcode[2], not_10_out, not_11_out);
  not not_11 (not_11_out, opcode[5]);
  not not_12 (not_12_out, opcode[0]);
  not not_13 (not_13_out, opcode[1]);
  not not_14 (not_14_out, opcode[4]);
  not not_15 (not_15_out, opcode[5]);
  not not_16 (not_16_out, Ori);
  nor nor_1 (nor_1_out, and_3_out, and_1_out);
  not not_17 (not_17_out, opcode[3]);
  not not_18 (not_18_out, opcode[3]);
  not not_19 (not_19_out, opcode[0]);
  not not_20 (not_20_out, opcode[2]);
  not not_21 (not_21_out, opcode[1]);
  and and_6 (opALU1, not_15_out, not_14_out, not_18_out, not_20_out, not_21_out, not_19_out);
  and and_7 (ExtOp, not_16_out, nor_1_out);
  and and_8 (MemToReg, not_17_out, opcode[5]);
  or or_2 (RegWr, opALU1, Or_Jal_out);

  assign RegDest = opALU1;

  // Other names for the same wires on the sheet: _0 = opcode[0]; _1 = opcode[1]; _2 = opcode[2]; _3 = opcode[3];
  //   _4 = opcode[4]; _5 = opcode[5]
endmodule

module ALUCtr (
  input  R_type,
  input  [5:0] opcode,
  input  [5:0] funct,
  output [5:0] ALUctl
);

  wire not_1_out, not_2_out, or_1_out, or_2_out;
  wire [2:0] and_2_out;

  not not_1 (not_1_out, opcode[3]);
  and and_1 (and_2_out[2], opcode[3], opcode[2], not_2_out);
  not not_2 (not_2_out, opcode[1]);
  or or_1 (or_1_out, opcode[3], opcode[5]);
  or or_2 (or_2_out, opcode[0], not_1_out);
  nor nor_1 (and_2_out[1], opcode[3], opcode[5]);
  and and_2 (and_2_out[0], or_1_out, or_2_out);
  Multiplexer #(.width(6), .enable("false")) multiplexer_1 (
    .in0({3'b100, and_2_out}), .in1(funct), .out(ALUctl), .sel(R_type));

  // Other names for the same wires on the sheet: _0 = opcode[0]; _1 = opcode[1]; _2 = opcode[2]; _3 = opcode[3];
  //   _4 = opcode[4]; _5 = opcode[5]
endmodule

module RegChooser (
  input  [4:0] register_num,
  output t0_t3
);

  wire comparator_1_lt, comparator_2_gt;

  Comparator #(.width(5), .mode("unsigned")) comparator_1 (
    .a(register_num), .b(5'b01100), .lt(comparator_1_lt));  // open: gt, eq
  Comparator #(.width(5), .mode("unsigned")) comparator_2 (
    .a(register_num), .b(5'b00111), .gt(comparator_2_gt));  // open: eq, lt
  and and_1 (t0_t3, comparator_1_lt, comparator_2_gt);
endmodule

module CorrectRegChoice (
  input  [31:0] from_run_circ,
  input  [31:0] from_regfile,
  input  [4:0] reg_num,
  output [31:0] correct_read_reg
);

  wire regchooser_1_t0_t3;

  RegChooser regchooser_1 (.register_num(reg_num), .t0_t3(regchooser_1_t0_t3));
  Multiplexer #(.width(32), .enable("false")) multiplexer_1 (
    .in0(from_run_circ), .in1(from_regfile), .out(correct_read_reg), .sel(regchooser_1_t0_t3));
endmodule

module WriteToCorrectReg (
  input  [4:0] RegNum,
  output [4:0] FormatRegNum,
  output wEnable_rf,
  output wEnable_run
);

  wire [4:0] subtractor_1_out;

  RegChooser regchooser_1 (.register_num(RegNum), .t0_t3(wEnable_rf));
  Subtractor #(.width(5)) subtractor_1 (.a(RegNum), .b(5'b01000), .out(subtractor_1_out));  // open: bin, bout
  Multiplexer #(.width(5), .enable("false")) multiplexer_1 (
    .in0(RegNum), .in1(subtractor_1_out), .out(FormatRegNum), .sel(wEnable_rf));
  not not_1 (wEnable_run, wEnable_rf);
endmodule

module sign_zero_extended (
  input  [5:0] opcode,
  input  [15:0] Immediate,
  input  ExtOp,
  output [31:0] ExtImm
);

  wire Lui;
  wire [31:0] bit_extender_1_out, bit_extender_2_out, multiplexer_1_out, shifter_1_out;

  Comparator #(.width(6), .mode("unsigned")) comparator_1 (.a(opcode), .b(6'b001111), .eq(Lui));  // open: gt, lt
  assign bit_extender_1_out = {{16{1'b0}}, Immediate};  // Bit_Extender bit_extender_1
  assign bit_extender_2_out = {{16{Immediate[15]}}, Immediate};  // Bit_Extender bit_extender_2
  Multiplexer #(.width(32), .enable("false")) multiplexer_1 (
    .in0(bit_extender_1_out), .in1(bit_extender_2_out), .out(multiplexer_1_out), .sel(ExtOp));
  Shifter #(.width(32)) shifter_1 (.in(multiplexer_1_out), .\dist (5'b10000), .out(shifter_1_out));
  Multiplexer #(.width(32), .enable("false")) multiplexer_2 (
    .in0(multiplexer_1_out), .in1(shifter_1_out), .out(ExtImm), .sel(Lui));
endmodule

module shamtUser (
  input  Rtype,
  input  [5:0] funct,
  input  [31:0] RT,
  input  [4:0] shamt,
  input  [31:0] RS,
  output [31:0] Y__RT_Shamt,
  output [31:0] X__RS_RT
);

  wire and_1_out, comparator_1_lt;
  wire [31:0] bit_extender_1_out;

  Comparator #(.width(6), .mode("unsigned")) comparator_1 (
    .a(funct), .b(6'b000100), .lt(comparator_1_lt));  // open: gt, eq
  assign bit_extender_1_out = {{27{1'b0}}, shamt};  // Bit_Extender bit_extender_1
  and and_1 (and_1_out, Rtype, comparator_1_lt);
  Multiplexer #(.width(32), .enable("false")) multiplexer_1 (
    .in0(RT), .in1(bit_extender_1_out), .out(Y__RT_Shamt), .sel(and_1_out));
  Multiplexer #(.width(32), .enable("false")) multiplexer_2 (.in0(RS), .in1(RT), .out(X__RS_RT), .sel(and_1_out));
endmodule
