// Logisim project regfile.circ as structural Verilog: 1 circuit, main circuit main
module main (
  input  [1:0] Read_register_1,
  input  [1:0] Read_register_2,
  input  [1:0] write_register,
  input  [31:0] write_data,
  input  RegWrite,
  input  clock,
  output [31:0] t0_Value,
  output [31:0] t1_Value,
  output [31:0] t2_Value,
  output [31:0] t3_Value,
  output [31:0] Read_Data_1,
  output [31:0] Read_Data_2
);

  wire demultiplexer_1_out0, demultiplexer_1_out1, demultiplexer_1_out2, demultiplexer_1_out3, t0, t1, t2, t3;

  Register #(.width(32)) register_1 (.D(write_data), .en(t0), .Q(t0_Value), .clk(clock));  // open: clr
  Demultiplexer #(.select(2), .enable("false")) demultiplexer_1 (
    .out0(demultiplexer_1_out0), .out1(demultiplexer_1_out1), .out2(demultiplexer_1_out2),
    .out3(demultiplexer_1_out3), .in(1'b1), .sel(write_register));
  Register #(.width(32)) register_2 (.D(write_data), .en(t1), .Q(t1_Value), .clk(clock));  // open: clr
  and and_1 (t0, demultiplexer_1_out0, RegWrite);
  and and_2 (t1, demultiplexer_1_out1, RegWrite);
  and and_3 (t2, demultiplexer_1_out2, RegWrite);
  and and_4 (t3, demultiplexer_1_out3, RegWrite);
  Register #(.width(32)) register_3 (.D(write_data), .en(t2), .Q(t2_Value), .clk(clock));  // open: clr
  Register #(.width(32)) register_4 (.D(write_data), .en(t3), .Q(t3_Value), .clk(clock));  // open: clr
  Multiplexer #(.select(2), .width(32), .enable("false")) multiplexer_1 (
    .in0(t0_Value), .in1(t1_Value), .in2(t2_Value), .in3(t3_Value), .out(Read_Data_1), .sel(Read_register_1));
  Multiplexer #(.select(2), .width(32), .enable("false")) multiplexer_2 (
    .in0(t0_Value), .in1(t1_Value), .in2(t2_Value), .in3(t3_Value), .out(Read_Data_2), .sel(Read_register_2));

  // Other names for the same wires on the sheet: Read_1[1:0] = Read_register_1; Read_2[1:0] = Read_register_2;
  //   t[31:0] = write_data; t0_out[31:0] = t0_Value; t1_out[31:0] = t1_Value; t2_out[31:0] = t2_Value;
  //   t3_out[31:0] = t3_Value; Write = RegWrite

  // Notes on the sheet:
  //   clock: pull=up
  //   These are INPUTS to the circuit
  //   These are INPUTS to the circuit
  //   DO NOT CHANGE THE LOCATIONS OF THE INPUTS/OUTPUTS! IF YOU DO SO, YOU NEED TO MAKE SURE THE PINS ARE AT THE RIGHT PLACE!
  //   These are OUTPUTS to the circuit
  //   Yet again, the clock is not an actual clock, but an input, one that will be driven from a higher circuit
  //   These are OUTPUTS to the circuit
endmodule
